# Fritzing sketch SKRIPSI (saved by Fritzing 0.9.2b)
breadboards: 2

parts:
  Raspberry_Pi_1 = Raspberry Pi 3 [part_number=RPI-3-V1.2]
  Pompa_Utama_5V = RELAY [package=relay-t9a]
  Pompa_Pengisap_5V = RELAY [package=relay-t9a]
  Pompa_Pengisi_5V = RELAY [package=relay-t9a]
  Lampu_Aquarium_5V = RELAY [package=relay-t9a]
  Suhu_Akuarium = DS18B20 1-Wire Temperature Sensor Module - 3 available pins [part_number=DS18B20]
  Suhu_Air_Cadangan = DS18B20 1-Wire Temperature Sensor Module - 3 available pins [part_number=DS18B20]
  Resistor_4_7K = Resistor [tolerance=±5% resistance=220 package="1206 [SMD]"]
  SENSOR_TURBIDITAS = RelayModule DFR0017
  Water_Lvl_Main_Tank = SRF05 Ultrasonic Rangefinder
  Water_Lvl_BackUp_Water = SRF05 Ultrasonic Rangefinder
  R1 = Resistor [tolerance=±5% resistance=220 package="1206 [SMD]"]
  R2 = Resistor [tolerance=±5% resistance=220 package="1206 [SMD]"]
  R3 = Resistor [tolerance=±5% resistance=220 package="1206 [SMD]"]
  R4 = Resistor [tolerance=±5% resistance=220 package="1206 [SMD]"]
  R5 = Resistor [tolerance=±5% resistance=220 package="1206 [SMD]"]
  R6 = Resistor [tolerance=±5% resistance=220 package="1206 [SMD]"]
  Part1 = Current Sensor 5A
  RelayModule_DFR1 = RelayModule DFR0017  # not connected
  Part2 = ADS1115  # not connected
  Part3 = ACS712 Current Sensor Module  # not connected

nets:
  VCC: Raspberry_Pi_1.3v3, Suhu_Akuarium.VCC, Suhu_Air_Cadangan.VCC, Resistor_4_7K.Pin_1
  N1: Raspberry_Pi_1.GIPO4, Suhu_Akuarium.DQ, Suhu_Air_Cadangan.DQ, Resistor_4_7K.Pin_0
  GND: Raspberry_Pi_1.GND, Suhu_Akuarium.GND, Suhu_Air_Cadangan.GND, Water_Lvl_Main_Tank.GND, Water_Lvl_BackUp_Water.GND, R2.Pin_1, R6.Pin_1, Part1.GND
  N2: Raspberry_Pi_1.GIPO17, Pompa_Utama_5V.MAIN
  N3: Raspberry_Pi_1.GIPO27, Pompa_Pengisap_5V.MAIN
  N4: Raspberry_Pi_1.GIPO22, Pompa_Pengisi_5V.MAIN
  N5: Raspberry_Pi_1.GIPO25, Water_Lvl_BackUp_Water.Trig
  N6: Raspberry_Pi_1.GIPO24, R4.Pin_0, R5.Pin_1
  N7: Raspberry_Pi_1.GIPO23, Lampu_Aquarium_5V.MAIN
  N8: Raspberry_Pi_1.GIPO15, Water_Lvl_Main_Tank.Trig
  N9: Raspberry_Pi_1.GIPO14, R1.Pin_0, R3.Pin_1
  VCC_2: Raspberry_Pi_1.5V, SENSOR_TURBIDITAS.5V, Water_Lvl_Main_Tank.VCC, Water_Lvl_BackUp_Water.VCC, Part1.VCC
  N10: Water_Lvl_Main_Tank.Echo, R1.Pin_1
  N11: Water_Lvl_BackUp_Water.Echo, R4.Pin_1
  N12: R2.Pin_0, R3.Pin_0
  N13: R5.Pin_0, R6.Pin_0

notes:
  Nanit pake ADC untuk ACS712 & DFROBOT

custom parts:
  DS18B20 1-Wire Temperature Sensor Module - 3 available pins: DS18B20 1-Wire Temperature Sensor Module ************* This module includes 4,7kΩ resistor
  ADS1115: ADC ADS1115
